# Fritzing sketch ESo8266-2.2TFTuSDCard (saved by Fritzing 0.9.3b)

parts:
  WeMos_D1_Mini1 = WeMos D1 Mini
  Part1 = TFT 2.2 inch 320x240 w microSD [part_number=1480]

nets:
  N1: WeMos_D1_Mini1.3V3, Part1.RESET
  5V: WeMos_D1_Mini1.5V, Part1.VIN
  N2: WeMos_D1_Mini1.D0, Part1.BACKLIGHT
  N3: WeMos_D1_Mini1.D6, Part1.MISO
  N4: WeMos_D1_Mini1.D8, Part1.LCDCS

custom parts:
  TFT 2.2 inch 320x240 w microSD: This lovely little display breakout is the best way to add a small, colorful and bright display to any project. Since the display uses 4-wire SPI to communicate and has its own pixel-addressable frame buffer, it can be used with every kind of microcontroller. Even a very small one with low memory and few pins available! The 2.2" display has 320x240 color pixels.
